# Fritzing sketch TempHumiditySensorLCD (saved by Fritzing 0.9.3b)
breadboards: 1

parts:
  Part1 = Arduino Nano (Rev3.0)
  RHT1 = Humidity and Temperature Sensor RHT03
  R1 = Resistor [tolerance=±5% resistance=10k package=THT]
  Nokia_5110_LCD_Module1 = Nokia 5110 LCD

nets:
  N1: Part1.GND, RHT1.GND_2, Nokia_5110_LCD_Module1.LED
  N2: Part1.D2, RHT1.Data-signal, R1.Pin_1
  N3: Part1.D3, Nokia_5110_LCD_Module1.VCC
  N4: Part1.D4, Nokia_5110_LCD_Module1.GND
  N5: Part1.D5, Nokia_5110_LCD_Module1.SCE
  N6: Part1.D6, Nokia_5110_LCD_Module1.RST
  N7: Part1.D7, Nokia_5110_LCD_Module1.D/C
  5V: Part1.5V, RHT1.Vcc, R1.Pin_0, Nokia_5110_LCD_Module1.DN(MOSI), Nokia_5110_LCD_Module1.DN(MODI)_(out)
  N8: Part1.3V3, Nokia_5110_LCD_Module1.SCLK, Nokia_5110_LCD_Module1.SCLK_(out)

custom parts:
  Nokia 5110 LCD: Nokia 5110 Graphic 84*48 LCD module such as the Sparkfun LCD-10168 or the clones from Ebay. There is example code for the Arduino available from the Sparkfun site in https://learn.sparkfun.com/tutorials/graphic-lcd-hookup-guide This is a 3.3V device, if you are running it from a 5V micro you need a 5V tolorant level translator such as the 74ahc367 to protect the signal imputs. Rafa G. did a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
